# Fritzing sketch Schematic (saved by Fritzing 0.9.3b)
breadboards: 1

parts:
  LCD1 = LCD screen
  Part1 = Arduino Mega 2560 (Rev3)
  Matrix_keypad1 = KEYPAD 4x4
  R1 = Rotary Potentiometer (Small) [maximum_resistance=100kΩ package=THT]
  S1 = Pushbutton [package="[THT]"]
  S2 = Pushbutton [package="[THT]"]
  S3 = Pushbutton [package="[THT]"]
  S4 = Pushbutton [package="[THT]"]
  S5 = Pushbutton [package="[THT]"]
  S6 = Pushbutton [package="[THT]"]
  LED1 = LED - 5mm [color="Red (633nm)" package="5 mm [THT]"]
  LED2 = LED - 5mm [color="Green (560nm)" package="5 mm [THT]"]
  LED3 = LED - 5mm [color="Blue (470nm)" package="5 mm [THT]"]
  R2 = Resistor [tolerance=±5% resistance=220 package=THT]
  R3 = Resistor [tolerance=±5% resistance=220 package=THT]
  R4 = Resistor [tolerance=±5% resistance=220 package=THT]
  S7 = Pushbutton [package="[THT]"]

nets:
  VSS: LCD1.VSS, LCD1.R/W, LCD1.LED-, Part1.GND, R1.leg2, S1.Pin_3, S1.Pin_4, S2.Pin_3, S2.Pin_4, S3.Pin_3, S3.Pin_4, S4.Pin_3, S4.Pin_4, S5.Pin_3, S5.Pin_4, S6.Pin_3, S6.Pin_4, LED1.cathode, LED2.cathode, LED3.cathode, S7.Pin_3, S7.Pin_4
  VDD: LCD1.VDD, LCD1.LED+, Part1.5V, R1.leg1
  N1: LCD1.V0, R1.wiper
  N2: LCD1.RS, Part1.D7_PWM
  N3: LCD1.E, Part1.D8_PWM
  N4: LCD1.DB4, Part1.D9_PWM
  N5: LCD1.DB5, Part1.D12_PWM
  N6: LCD1.DB6, Part1.D11_PWM
  N7: LCD1.DB7, Part1.D10_PWM
  N8: Part1.D36, R4.Pin_0
  N9: Part1.D37, R3.Pin_0
  N10: Part1.D38, R2.Pin_0
  N11: Part1.D39, S7.Pin_1, S7.Pin_2
  N12: Part1.D40, S6.Pin_1, S6.Pin_2
  N13: Part1.D41, S5.Pin_1, S5.Pin_2
  N14: Part1.D42, S4.Pin_1, S4.Pin_2
  N15: Part1.D43, S3.Pin_1, S3.Pin_2
  N16: Part1.D44, S2.Pin_1, S2.Pin_2
  N17: Part1.D45, S1.Pin_1, S1.Pin_2
  N18: Part1.D46, Matrix_keypad1.row4
  N19: Part1.D47, Matrix_keypad1.row3
  N20: Part1.D48, Matrix_keypad1.row2
  N21: Part1.D49, Matrix_keypad1.row1
  N22: Part1.D50, Matrix_keypad1.col4
  N23: Part1.D51, Matrix_keypad1.col3
  N24: Part1.D52, Matrix_keypad1.col2
  N25: Part1.D53, Matrix_keypad1.col1
  N26: LED1.anode, R4.Pin_1
  N27: LED2.anode, R3.Pin_1
  N28: LED3.anode, R2.Pin_1

custom parts:
  KEYPAD 4x4: Matrix keypad 16 buttons, 4 rows x 4 columns
